// Logisim project dani_proyecto1.circ as structural Verilog: 4 circuits, main circuit transcod_puertas
module transcod_puertas (
  input  X0,
  input  X1,
  input  X2,
  input  X3,
  output E,
  output C,
  output A,
  output F,
  output D,
  output B,
  output G
);

  wire and_1_out, and_2_out, and_3_out, and_4_out, and_5_out, and_6_out, and_7_out, and_8_out, and_9_out,
       and_10_out, and_11_out, and_12_out, and_13_out, and_14_out, and_15_out, and_16_out, and_17_out,
       and_18_out, and_19_out, and_20_out, and_21_out, and_22_out, and_23_out, and_24_out, and_25_out,
       and_26_out, and_27_out, and_28_out, and_29_out, and_30_out, and_31_out, and_32_out, and_33_out,
       and_34_out, and_35_out, tnX0, tnX1, tnX2, tnX3;

  not not_1 (tnX0, X0);
  not not_2 (tnX1, X1);
  not not_3 (tnX2, X2);
  not not_4 (tnX3, X3);
  and and_1 (and_1_out, tnX2, tnX0);
  and and_2 (and_2_out, tnX3, X1);
  and and_3 (and_3_out, tnX3, X2, X0);
  and and_4 (and_4_out, X2, X1);
  and and_5 (and_5_out, X3, tnX0);
  and and_6 (and_6_out, X3, tnX2, tnX1);
  and and_7 (and_7_out, X3, tnX1, X0);
  and and_8 (and_8_out, tnX2, tnX0);
  and and_9 (and_9_out, tnX3, tnX1, tnX0);
  and and_10 (and_10_out, tnX3, X1, X0);
  and and_11 (and_11_out, tnX3, tnX2);
  or or_1 (A, and_1_out, and_2_out, and_3_out, and_4_out, and_5_out, and_6_out);
  or or_2 (B, and_7_out, and_8_out, and_9_out, and_10_out, and_11_out);
  and and_12 (and_12_out, tnX1, X0);
  and and_13 (and_13_out, tnX3, X2);
  and and_14 (and_14_out, X3, tnX2);
  and and_15 (and_15_out, tnX3, tnX1);
  and and_16 (and_16_out, tnX3, X0);
  and and_17 (and_17_out, X2, tnX1, X0);
  and and_18 (and_18_out, tnX2, X1, X0);
  and and_19 (and_19_out, X2, X1, tnX0);
  and and_20 (and_20_out, X3, tnX1);
  and and_21 (and_21_out, tnX3, tnX2, tnX0);
  or or_3 (C, and_12_out, and_13_out, and_14_out, and_15_out, and_16_out);
  or or_4 (D, and_17_out, and_18_out, and_19_out, and_20_out, and_21_out);
  and and_22 (and_22_out, tnX2, tnX0);
  and and_23 (and_23_out, X1, tnX0);
  and and_24 (and_24_out, X3, X1);
  and and_25 (and_25_out, X3, X2);
  and and_26 (and_26_out, tnX1, tnX0);
  and and_27 (and_27_out, X2, tnX0);
  and and_28 (and_28_out, tnX3, X2, tnX1);
  and and_29 (and_29_out, X3, tnX2);
  and and_30 (and_30_out, X3, X1);
  and and_31 (and_31_out, tnX2, X1);
  and and_32 (and_32_out, X3, tnX2);
  and and_33 (and_33_out, X3, X0);
  and and_34 (and_34_out, X1, tnX0);
  and and_35 (and_35_out, tnX3, X2, tnX1);
  or or_5 (E, and_22_out, and_23_out, and_24_out, and_25_out);
  or or_6 (F, and_26_out, and_27_out, and_28_out, and_29_out, and_30_out);
  or or_7 (G, and_31_out, and_32_out, and_33_out, and_34_out, and_35_out);

  // Other names for the same wires on the sheet: tX0 = X0; tX1 = X1; tX2 = X2; tX3 = X3
endmodule

module transcod_puertas_test (
  input  [3:0] InputBinary
);

  wire tA, tB, tC, tD, tE, tF, tG;

  _7_Segment_Display u_7_segment_display_1 (.g(tG), .f(tF), .a(tA), .b(tB), .e(tE), .d(tD), .c(tC));  // open: dp
  transcod_puertas transcod_puertas_1 (
    .X0(InputBinary[0]), .X1(InputBinary[1]), .X2(InputBinary[2]), .X3(InputBinary[3]), .E(tE), .C(tC),
    .A(tA), .F(tF), .D(tD), .B(tB), .G(tG));
endmodule

module transcod_PLA (
  input  [3:0] Entrada,
  output [6:0] Salida
);

  // PlaRom #(.Contents("1*7 2 1 1 2 1*3 2 2 1 2 1*3 2 1 2 1 2 2 1 1 2*4 1*3 2 1 1 2 2 1 2 1 2 1 2*4 1 1 2 2 1 2*4 1 2*4 1*6 0 0 1 1 0*4 1 1 0 1 1 0 1*5 0 0 1 0 1 1 0 0 1*3 0 1 1 0 1 1 0 0 1*8 0*4 1*10 0 0 1*5 0 1*3 0 0 1*6 0 0 1*3 0 0 1*4 0 1 1 0 0 1*5 0*3 1*3"), .\and (16), .outputs(7)) plarom_1: pin names not known; wires that end beside it: Entrada, Salida
endmodule

module transcod_PLA_test (
  input  [3:0] Entrada
);

  wire tA, tB, tC, tD, tE, tF, tG;

  _7_Segment_Display u_7_segment_display_1 (.g(tG), .f(tF), .a(tA), .b(tB), .e(tE), .d(tD), .c(tC));  // open: dp
  transcod_PLA transcod_pla_1 (.Entrada(Entrada), .Salida({tA, tB, tC, tD, tE, tF, tG}));
endmodule
