// Logisim project proyecto1_grupo3.circ.circ as structural Verilog: 21 circuits, main circuit contador_FSM
module contador_FSM (
  input  Clk,
  input  Clear,
  output Q3,
  output Q2,
  output Q1,
  output Q0
);

  wire cirq0_1_out_2, cirq1_1_out_5, cirq2_1_out_5, cirq3_1_out_5;

  cirQ3 cirq3_1 (.q3(Q3), .q2(Q2), .q1(Q1), .q0(Q0), .out_5(cirq3_1_out_5));
  cirQ2 cirq2_1 (.q3(Q3), .q2(Q2), .q1(Q1), .q0(Q0), .out_5(cirq2_1_out_5));
  cirQ1 cirq1_1 (.q3(Q3), .q2(Q2), .q1(Q1), .q0(Q0), .out_5(cirq1_1_out_5));
  cirQ0 cirq0_1 (.q0(Q0), .out_2(cirq0_1_out_2));
  D_Flip_Flop d_ff_1 (.D(cirq3_1_out_5), .clk(Clk), .Q(Q3), .reset(Clear));  // open: Qn, preset
  D_Flip_Flop d_ff_2 (.D(cirq2_1_out_5), .clk(Clk), .Q(Q2), .reset(Clear));  // open: Qn, preset
  D_Flip_Flop d_ff_3 (.D(cirq1_1_out_5), .clk(Clk), .Q(Q1), .reset(Clear));  // open: Qn, preset
  D_Flip_Flop d_ff_4 (.D(cirq0_1_out_2), .clk(Clk), .Q(Q0), .reset(Clear));  // open: Qn, preset
endmodule

module cirQ3 (
  input  q3,
  input  q2,
  input  q1,
  input  q0,
  output out_5
);

  wire and_1_out, and_2_out, and_3_out, and_4_out, not_1_out, not_2_out;

  not not_1 (not_1_out, q2);
  not not_2 (not_2_out, q0);
  and and_1 (and_1_out, q2, q1);
  and and_2 (and_2_out, q3, not_2_out, q2);
  and and_3 (and_3_out, q3, not_1_out, q0);
  and and_4 (and_4_out, q3, q1);
  or or_1 (out_5, and_1_out, and_2_out, and_3_out, and_4_out);
endmodule

module cirQ2 (
  input  q3,
  input  q2,
  input  q1,
  input  q0,
  output out_5
);

  wire and_1_out, and_2_out, and_3_out, and_4_out, and_5_out, not_1_out, not_2_out, not_3_out, not_4_out;

  not not_1 (not_1_out, q3);
  not not_2 (not_2_out, q2);
  not not_3 (not_3_out, q1);
  not not_4 (not_4_out, q0);
  and and_1 (and_1_out, q3, q2, q1, q0);
  and and_2 (and_2_out, q2, not_3_out, not_4_out);
  and and_3 (and_3_out, q3, not_2_out, not_4_out);
  and and_4 (and_4_out, not_1_out, not_2_out, q0);
  and and_5 (and_5_out, q3, not_2_out, not_3_out);
  or or_1 (out_5, and_1_out, and_2_out, and_3_out, and_4_out, and_5_out);
endmodule

module cirQ1 (
  input  q3,
  input  q2,
  input  q1,
  input  q0,
  output out_5
);

  wire and_1_out, and_2_out, and_3_out, and_4_out, and_5_out, not_1_out, not_2_out, not_3_out;

  not not_1 (not_1_out, q3);
  not not_2 (not_2_out, q1);
  not not_3 (not_3_out, q0);
  and and_1 (and_1_out, not_1_out, not_2_out, not_3_out);
  and and_2 (and_2_out, not_1_out, q1, q0);
  and and_3 (and_3_out, not_1_out, q2, not_2_out);
  and and_4 (and_4_out, q3, q2, not_3_out);
  and and_5 (and_5_out, q3, q2, q1);
  or or_1 (out_5, and_1_out, and_2_out, and_3_out, and_4_out, and_5_out);
endmodule

module cirQ0 (
  input  q0,
  output out_2
);

  not not_1 (out_2, q0);
endmodule

module contador_FSM_test (
  input  Clear
);

  wire Clk_out;
  wire [3:0] binary_to_bcd_converter_1_p2, binary_to_bcd_converter_1_p3, contador_fsm_1_q0;

  Clock Clk (.out(Clk_out));
  contador_FSM contador_fsm_1 (
    .Clk(Clk_out), .Clear(Clear), .Q3(contador_fsm_1_q0[3]), .Q2(contador_fsm_1_q0[2]),
    .Q1(contador_fsm_1_q0[1]), .Q0(contador_fsm_1_q0[0]));
  Hex_Digit_Display hex_digit_display_1 (.value(binary_to_bcd_converter_1_p2));  // open: dp
  Hex_Digit_Display hex_digit_display_2 (.value(binary_to_bcd_converter_1_p3));  // open: dp
  // Binary_to_BCD_converter #(.binvalue(4)) binary_to_bcd_converter_1: pin names not known; wires that end beside it: contador_fsm_1_q0, binary_to_bcd_converter_1_p2, binary_to_bcd_converter_1_p3
endmodule

module cq3 (
  input  E_3,
  input  E_2,
  input  E_1,
  input  E_0,
  output Q_3
);

  wire and_1_out, and_2_out, and_3_out, and_4_out, not_1_out, not_2_out, not_3_out, not_4_out;

  not not_1 (not_1_out, E_3);
  not not_2 (not_2_out, E_2);
  not not_3 (not_3_out, E_1);
  not not_4 (not_4_out, E_0);
  and and_1 (and_1_out, E_3, not_2_out, not_3_out, not_4_out);
  and and_2 (and_2_out, not_1_out, E_1, E_0);
  and and_3 (and_3_out, not_1_out, E_2);
  and and_4 (and_4_out, E_2, E_1);
  or or_1 (Q_3, and_1_out, and_2_out, and_3_out, and_4_out);
endmodule

module cq2 (
  input  E_3,
  input  E_2,
  input  E_1,
  input  E_0,
  output Q_2
);

  wire and_1_out, and_2_out, and_3_out, and_4_out, not_1_out, not_2_out, not_3_out;

  not not_1 (not_1_out, E_3);
  not not_2 (not_2_out, E_1);
  not not_3 (not_3_out, E_0);
  and and_1 (and_1_out, not_1_out, E_1, not_3_out);
  and and_2 (and_2_out, E_3, E_2, E_0);
  and and_3 (and_3_out, E_2, not_2_out);
  and and_4 (and_4_out, E_3, not_2_out, E_0);
  or or_1 (Q_2, and_1_out, and_2_out, and_3_out, and_4_out);
endmodule

module cq1 (
  input  E_3,
  input  E_2,
  input  E_1,
  input  E_0,
  output Q_1
);

  wire and_1_out, and_2_out, and_3_out, and_4_out, not_1_out, not_2_out, not_3_out;

  not not_1 (not_1_out, E_3);
  not not_2 (not_2_out, E_1);
  not not_3 (not_3_out, E_0);
  and and_1 (and_1_out, not_1_out, not_2_out, E_0);
  and and_2 (and_2_out, E_1, not_3_out);
  and and_3 (and_3_out, E_2, not_2_out, E_0);
  and and_4 (and_4_out, not_1_out, E_2, E_1);
  or or_1 (Q_1, and_1_out, and_2_out, and_3_out, and_4_out);
endmodule

module cq0 (
  input  E_0,
  output Q_0
);


  assign Q_0 = E_0;
endmodule

module contador_opt (
  input  Reset,
  input  Clk,
  output Q_3,
  output Q_2,
  output Q_1,
  output Q_0
);

  wire tq0, tq1, tq2, tq3;

  Counter #(.max('hf), .width(4)) counter_1 (
    .clr(Reset), .load(1'b0), .up(1'b1), .count(1'b1), .clk(Clk), .Q({tq3, tq2, tq1, tq0}));  // open: D, carry
  cq3 cq3_1 (.E_3(tq3), .E_2(tq2), .E_1(tq1), .E_0(tq0), .Q_3(Q_3));
  cq2 cq2_1 (.E_3(tq3), .E_2(tq2), .E_1(tq1), .E_0(tq0), .Q_2(Q_2));
  cq1 cq1_1 (.E_3(tq3), .E_2(tq2), .E_1(tq1), .E_0(tq0), .Q_1(Q_1));
  cq0 cq0_1 (.E_0(tq0), .Q_0(Q_0));
endmodule

module contador_opt_test (
  input  Reset
);

  wire Clk_out;
  wire [3:0] binary_to_bcd_converter_1_p2, binary_to_bcd_converter_1_p3, contador_opt_1_q_0;

  Clock Clk (.out(Clk_out));
  contador_opt contador_opt_1 (
    .Reset(Reset), .Clk(Clk_out), .Q_3(contador_opt_1_q_0[3]), .Q_2(contador_opt_1_q_0[2]),
    .Q_1(contador_opt_1_q_0[1]), .Q_0(contador_opt_1_q_0[0]));
  Hex_Digit_Display hex_digit_display_1 (.value(binary_to_bcd_converter_1_p2));  // open: dp
  // Binary_to_BCD_converter #(.binvalue(4)) binary_to_bcd_converter_1: pin names not known; wires that end beside it: contador_opt_1_q_0, binary_to_bcd_converter_1_p2, binary_to_bcd_converter_1_p3
  Hex_Digit_Display hex_digit_display_2 (.value(binary_to_bcd_converter_1_p3));  // open: dp
endmodule

module transcod_puertas (
  input  X0,
  input  X1,
  input  X2,
  input  X3,
  output E,
  output C,
  output A,
  output G,
  output B,
  output D,
  output F
);

  wire and_1_out, and_2_out, and_3_out, and_4_out, and_5_out, and_6_out, and_7_out, and_8_out, and_9_out,
       and_10_out, and_11_out, and_12_out, and_13_out, and_14_out, and_15_out, and_16_out, and_17_out,
       and_18_out, and_19_out, and_20_out, and_21_out, and_22_out, and_23_out, and_24_out, and_25_out,
       and_26_out, and_27_out, and_28_out, and_29_out, and_30_out, and_31_out, and_32_out, and_33_out,
       and_34_out, and_35_out, tnX0, tnX1, tnX2, tnX3;

  not not_1 (tnX0, X0);
  not not_2 (tnX1, X1);
  not not_3 (tnX2, X2);
  not not_4 (tnX3, X3);
  and and_1 (and_1_out, tnX2, X1);
  and and_2 (and_2_out, X3, tnX2);
  and and_3 (and_3_out, X3, X0);
  and and_4 (and_4_out, X1, tnX0);
  and and_5 (and_5_out, tnX3, X2, tnX1);
  or or_1 (G, and_1_out, and_2_out, and_3_out, and_4_out, and_5_out);
  and and_6 (and_6_out, tnX2, tnX0);
  and and_7 (and_7_out, tnX3, X1);
  and and_8 (and_8_out, tnX3, X2, X0);
  and and_9 (and_9_out, X2, X1);
  and and_10 (and_10_out, X3, tnX0);
  and and_11 (and_11_out, X3, tnX2, tnX1);
  and and_12 (and_12_out, X3, tnX1, X0);
  and and_13 (and_13_out, tnX2, tnX0);
  and and_14 (and_14_out, tnX3, tnX1, tnX0);
  and and_15 (and_15_out, tnX3, X1, X0);
  and and_16 (and_16_out, tnX3, tnX2);
  or or_2 (A, and_6_out, and_7_out, and_8_out, and_9_out, and_10_out, and_11_out);
  or or_3 (B, and_12_out, and_13_out, and_14_out, and_15_out, and_16_out);
  and and_17 (and_17_out, tnX1, X0);
  and and_18 (and_18_out, tnX3, X2);
  and and_19 (and_19_out, X3, tnX2);
  and and_20 (and_20_out, tnX3, tnX1);
  and and_21 (and_21_out, tnX3, X0);
  and and_22 (and_22_out, X2, tnX1, X0);
  and and_23 (and_23_out, tnX2, X1, X0);
  and and_24 (and_24_out, X2, X1, tnX0);
  and and_25 (and_25_out, X3, tnX1);
  and and_26 (and_26_out, tnX3, tnX2, tnX0);
  or or_4 (C, and_17_out, and_18_out, and_19_out, and_20_out, and_21_out);
  or or_5 (D, and_22_out, and_23_out, and_24_out, and_25_out, and_26_out);
  and and_27 (and_27_out, tnX2, tnX0);
  and and_28 (and_28_out, X1, tnX0);
  and and_29 (and_29_out, X3, X1);
  and and_30 (and_30_out, X3, X2);
  and and_31 (and_31_out, tnX1, tnX0);
  and and_32 (and_32_out, X2, tnX0);
  and and_33 (and_33_out, tnX3, X2, tnX1);
  and and_34 (and_34_out, X3, tnX2);
  and and_35 (and_35_out, X3, X1);
  or or_6 (E, and_27_out, and_28_out, and_29_out, and_30_out);
  or or_7 (F, and_31_out, and_32_out, and_33_out, and_34_out, and_35_out);

  // Other names for the same wires on the sheet: tX0 = X0; tX1 = X1; tX2 = X2; tX3 = X3
endmodule

module transcod_puertas_test (
  input  [3:0] InputBinary
);

  wire tA, tB, tC, tD, tE, tF, tG;

  transcod_puertas transcod_puertas_1 (
    .X0(InputBinary[0]), .X1(InputBinary[1]), .X2(InputBinary[2]), .X3(InputBinary[3]), .E(tE), .C(tC),
    .A(tA), .G(tG), .B(tB), .D(tD), .F(tF));
  _7_Segment_Display u_7_segment_display_1 (.g(tG), .f(tF), .a(tA), .b(tB), .e(tE), .d(tD), .c(tC));  // open: dp
endmodule

module transcod_PLA (
  input  [3:0] Entrada,
  output [6:0] Salida
);

  // PlaRom #(.Contents("1*7 2 1 1 2 1*3 2 2 1 2 1*3 2 1 2 1 2 2 1 1 2*4 1*3 2 1 1 2 2 1 2 1 2 1 2*4 1 1 2 2 1 2*4 1 2*4 1*6 0 0 1 1 0*4 1 1 0 1 1 0 1*5 0 0 1 0 1 1 0 0 1*3 0 1 1 0 1 1 0 0 1*8 0*4 1*10 0 0 1*5 0 1*3 0 0 1*6 0 0 1*3 0 0 1*4 0 1 1 0 0 1*5 0*3 1*3"), .\and (16), .outputs(7)) plarom_1: pin names not known; wires that end beside it: Entrada, Salida
endmodule

module transcod_PLA_test (
  input  [3:0] Entrada
);

  wire tA, tB, tC, tD, tE, tF, tG;

  transcod_PLA transcod_pla_1 (.Entrada(Entrada), .Salida({tA, tB, tC, tD, tE, tF, tG}));
  _7_Segment_Display u_7_segment_display_1 (.g(tG), .f(tF), .a(tA), .b(tB), .e(tE), .d(tD), .c(tC));  // open: dp
endmodule

module circuito_final (
  input  Clear
);

  wire Clk_out, tAf, tBf, tCf, tDf, tEf, tFf, tGf;
  wire [3:0] contador_fsm_1_q3;

  Clock Clk (.out(Clk_out));
  contador_FSM contador_fsm_1 (
    .Clk(Clk_out), .Clear(Clear), .Q3(contador_fsm_1_q3[0]), .Q2(contador_fsm_1_q3[1]),
    .Q1(contador_fsm_1_q3[2]), .Q0(contador_fsm_1_q3[3]));
  transcod_PLA transcod_pla_1 (.Entrada(contador_fsm_1_q3), .Salida({tAf, tBf, tCf, tDf, tEf, tFf, tGf}));
  _7_Segment_Display u_7_segment_display_1 (.g(tGf), .f(tFf), .a(tAf), .b(tBf), .e(tEf), .d(tDf), .c(tCf));  // open: dp
endmodule

module transcod_ROM (
  input  [3:0] Entrada,
  output x,
  output A,
  output B,
  output C,
  output D,
  output E,
  output F,
  output G
);

  ROM #(.addrWidth(4)) rom_1 (.addr(Entrada), .data({x, A, B, C, D, E, F, G}));

  // Notes on the sheet:
  //   contents of rom_1 (hex, n*v repeats v):
  //   7e 30 6d 79 33 5b 5f 70 7f 7b 77 1f 4e 3d 4f 47
endmodule

module transcod_ROM_test (
  input  [3:0] Entrada
);

  wire A, B, C, D, E, F, G;

  transcod_ROM transcod_rom_1 (.Entrada(Entrada), .A(A), .B(B), .C(C), .D(D), .E(E), .F(F), .G(G));  // open: x
  _7_Segment_Display u_7_segment_display_1 (.g(G), .f(F), .a(A), .b(B), .e(E), .d(D), .c(C));  // open: dp
endmodule

module transcod_deco (
  input  Enable,
  input  x0,
  input  x1,
  input  x2,
  input  x3,
  output A,
  output B,
  output C,
  output D,
  output E,
  output F,
  output G
);

  wire deco0, deco1, deco2, deco3, deco4, deco5, deco6, deco7, deco8, deco9, decoA, decoB, decoC, decoD,
       decoE, decoF;

  Decoder #(.select(4)) decoder_1 (
    .out0(deco0), .out1(deco1), .out2(deco2), .out3(deco3), .out4(deco4), .out5(deco5), .out6(deco6),
    .out7(deco7), .out8(deco8), .out9(deco9), .out10(decoA), .out11(decoB), .out12(decoC), .out13(decoD),
    .out14(decoE), .out15(decoF), .sel({x3, x2, x1, x0}), .en(Enable));
  or or_1 (A, deco0, deco2, deco3, deco5, deco6, deco7, deco8, deco9, decoA, decoC, decoE, decoF);
  or or_2 (B, deco0, deco1, deco2, deco3, deco4, deco7, deco8, deco9, decoA, decoD);
  or or_3 (C, deco0, deco1, deco3, deco4, deco5, deco6, deco7, deco8, deco9, decoA, decoB, decoD);
  or or_4 (D, deco0, deco2, deco3, deco5, deco6, deco8, deco9, decoB, decoC, decoD, decoE);
  or or_5 (E, deco0, deco2, deco6, deco8, decoA, decoB, decoC, decoD, decoE, decoF);
  or or_6 (F, deco0, deco4, deco5, deco6, deco8, deco9, decoA, decoB, decoC, decoE, decoF);
  or or_7 (G, deco2, deco3, deco4, deco5, deco6, deco8, deco9, decoA, decoB, decoD, decoE, decoF);
endmodule

module transcod_deco_test (
  input  Enable,
  input  [3:0] Entrada
);

  wire A, B, C, D, E, F, G;

  transcod_deco transcod_deco_1 (
    .Enable(Enable), .x0(Entrada[0]), .x1(Entrada[1]), .x2(Entrada[2]), .x3(Entrada[3]), .A(A), .B(B), .C(C),
    .D(D), .E(E), .F(F), .G(G));
  _7_Segment_Display u_7_segment_display_1 (.g(G), .f(F), .a(A), .b(B), .e(E), .d(D), .c(C));  // open: dp
endmodule
