// Logisim project registro.circ as structural Verilog: 1 circuit, main circuit main
module main (
  input  WE,
  input  Clear,
  output [3:0] Z
);

  wire Clk_out;
  wire [3:0] D3_out;

  Clock #(.highDuration(4)) D3 (.out(D3_out[0]));
  Clock #(.highDuration(3)) D2 (.out(D3_out[1]));
  Clock #(.highDuration(2), .lowDuration(2)) D1 (.out(D3_out[2]));
  Clock D0 (.out(D3_out[3]));
  Clock Clk (.out(Clk_out));
  Register #(.width(4)) register_1 (.D(D3_out), .en(WE), .clk(Clk_out), .Q(Z), .clr(Clear));
  Hex_Digit_Display hex_digit_display_1 (.value(Z));  // open: dp
endmodule
