// Logisim project trans_op_1.circ as structural Verilog: 4 circuits, main circuit transcod_ROM
module transcod_ROM (
  input  [3:0] in_1,
  output x,
  output A,
  output B,
  output C,
  output D,
  output E,
  output F,
  output G
);

  ROM #(.addrWidth(4)) rom_1 (.addr(in_1), .data({x, A, B, C, D, E, F, G}));

  // Notes on the sheet:
  //   contents of rom_1 (hex, n*v repeats v):
  //   7e 30 6d 79 33 5b 5f 70 7f 7b 77 1f 4e 3d 4f 47
endmodule

module transcod_ROM_test (
);

  wire A, B, C, D, E, F, G;
  wire [3:0] clock_1_out;

  Clock clock_1 (.out(clock_1_out[0]));
  Clock #(.highDuration(2), .lowDuration(2)) clock_2 (.out(clock_1_out[1]));
  Clock #(.highDuration(4), .lowDuration(4)) clock_3 (.out(clock_1_out[2]));
  Clock #(.highDuration(8), .lowDuration(8)) clock_4 (.out(clock_1_out[3]));
  transcod_ROM transcod_rom_1 (.in_1(clock_1_out), .A(A), .B(B), .C(C), .D(D), .E(E), .F(F), .G(G));  // open: x
  _7_Segment_Display u_7_segment_display_1 (.g(G), .f(F), .a(A), .b(B), .e(E), .d(D), .c(C));  // open: dp
endmodule

module transcod_deco (
  input  Enable,
  input  x0,
  input  x1,
  input  x2,
  input  x3,
  output A,
  output B,
  output C,
  output D,
  output E,
  output F,
  output G
);

  wire deco0, deco1, deco2, deco3, deco4, deco5, deco6, deco7, deco8, deco9, decoA, decoB, decoC, decoD,
       decoE, decoF;

  Decoder #(.select(4)) decoder_1 (
    .out0(deco0), .out1(deco1), .out2(deco2), .out3(deco3), .out4(deco4), .out5(deco5), .out6(deco6),
    .out7(deco7), .out8(deco8), .out9(deco9), .out10(decoA), .out11(decoB), .out12(decoC), .out13(decoD),
    .out14(decoE), .out15(decoF), .sel({x3, x2, x1, x0}), .en(Enable));
  or or_1 (A, deco0, deco2, deco3, deco5, deco6, deco7, deco8, deco9, decoA, decoC, decoE, decoF);
  or or_2 (B, deco0, deco1, deco2, deco3, deco4, deco7, deco8, deco9, decoA, decoD);
  or or_3 (C, deco0, deco1, deco3, deco4, deco5, deco6, deco7, deco8, deco9, decoA, decoB, decoD);
  or or_4 (D, deco0, deco2, deco3, deco5, deco6, deco8, deco9, decoB, decoC, decoD, decoE);
  or or_5 (E, deco0, deco2, deco6, deco8, decoA, decoB, decoC, decoD, decoE, decoF);
  or or_6 (F, deco0, deco4, deco5, deco6, deco8, deco9, decoA, decoB, decoC, decoE, decoF);
  or or_7 (G, deco2, deco3, deco4, deco5, deco6, deco8, deco9, decoA, decoB, decoD, decoE, decoF);
endmodule

module transcod_deco_test (
  input  in_1
);

  wire A, B, C, clock_1_out, clock_2_out, clock_3_out, clock_4_out, D, E, F, G;

  Clock clock_1 (.out(clock_1_out));
  Clock #(.highDuration(2), .lowDuration(2)) clock_2 (.out(clock_2_out));
  Clock #(.highDuration(4), .lowDuration(4)) clock_3 (.out(clock_3_out));
  Clock #(.highDuration(8), .lowDuration(8)) clock_4 (.out(clock_4_out));
  transcod_deco transcod_deco_1 (
    .Enable(in_1), .x0(clock_1_out), .x1(clock_2_out), .x2(clock_3_out), .x3(clock_4_out), .A(A), .B(B),
    .C(C), .D(D), .E(E), .F(F), .G(G));
  _7_Segment_Display u_7_segment_display_1 (.g(G), .f(F), .a(A), .b(B), .e(E), .d(D), .c(C));  // open: dp
endmodule
